// Logisim project DD1_Alarm_Clock_final.circ as structural Verilog: 1 circuit, main circuit main
module main (
);

  wire AH1_carry, AH2_carry, AM2_carry, and_1_out, and_2_out, and_3_out, and_4_out, and_5_out, and_6_out,
       and_7_out, and_8_out, and_9_out, and_10_out, and_11_out, and_12_out, and_13_out, and_14_out,
       and_15_out, and_16_out, and_17_out, and_18_out, and_19_out, and_20_out, and_21_out, and_22_out,
       and_23_out, and_24_out, and_25_out, and_26_out, and_27_out, and_28_out, Center_out, clock_1_out,
       decoder_1_out0, decoder_1_out1, decoder_1_out2, decoder_1_out3, decoder_2_out0, decoder_2_out1,
       decoder_2_out2, decoder_2_out3, Down_out, Left_out, multiplexer_3_out, multiplexer_11_out, nor_1_out,
       nor_2_out, nor_3_out, nor_5_out, nor_6_out, nor_7_out, not_1_out, not_2_out, or_1_out, or_2_out,
       or_3_out, or_4_out, or_5_out, or_6_out, or_7_out, or_8_out, or_9_out, or_10_out, or_11_out, or_12_out,
       or_13_out, or_14_out, or_15_out, or_16_out, Right_out, S1_carry, S2_carry, t_ff_1_q, t_ff_2_q,
       t_ff_3_q, TH1_carry, TH2_carry, TM1_carry, TM2_carry, Up_out;
  wire [1:0] counter_1_q, counter_3_q;
  wire [3:0] AH1_q, AH2_q, AM1_q, AM2_q, bcd_to_7_segment_decoder_1_p1, bcd_to_7_segment_decoder_2_p1,
       bcd_to_7_segment_decoder_3_p1, bcd_to_7_segment_decoder_4_p1, multiplexer_1_out, multiplexer_2_out,
       multiplexer_6_out, multiplexer_7_out, multiplexer_9_out, multiplexer_10_out, multiplexer_13_out,
       multiplexer_14_out, multiplexer_15_out, nor_4_out, S1_q, S2_q, subtractor_1_out, subtractor_2_out,
       subtractor_3_out, subtractor_4_out, TH1_q, TH2_q, TM1_q, TM2_q;
  wire [6:0] counter_2_q;

  Button Left (.out(Left_out));
  Button Right (.out(Right_out));
  Button Center (.out(Center_out));
  Counter #(.max('h3), .width(2)) counter_1 (
    .up(Right_out), .count(or_1_out), .clk(counter_2_q[3]), .Q(counter_1_q));  // open: clr, load, D, carry
  or or_1 (or_1_out, Left_out, Right_out);
  or or_2 (or_2_out, Center_out, or_1_out, or_4_out);
  T_Flip_Flop t_ff_1 (.T(Center_out), .clk(counter_2_q[3]), .Q(t_ff_1_q));  // open: Qn, reset, preset
  Decoder #(.select(2)) decoder_1 (
    .out0(decoder_1_out0), .out1(decoder_1_out1), .out2(decoder_1_out2), .out3(decoder_1_out3),
    .sel(counter_1_q), .en(t_ff_1_q));
  Clock clock_1 (.out(clock_1_out));
  not not_1 (not_1_out, t_ff_1_q);
  Counter #(.max('h40), .width(7)) counter_2 (
    .count(1'b1), .clk(clock_1_out), .Q(counter_2_q));  // open: clr, load, up, D, carry
  or or_3 (or_3_out, decoder_1_out2, decoder_1_out3);
  Button Up (.out(Up_out));
  Button Down (.out(Down_out));
  not not_2 (not_2_out, Down_out);
  or or_4 (or_4_out, Up_out, Down_out);
  Multiplexer #(.width(4)) multiplexer_1 (.in0(4'b0000), .in1(4'b0011), .out(multiplexer_1_out), .sel(Down_out));
  Multiplexer #(.width(4)) multiplexer_2 (.in0(4'b0000), .in1(4'b0010), .out(multiplexer_2_out), .sel(Down_out));
  Counter #(.max('h9), .width(4)) S2 (
    .clr(t_ff_1_q), .count(1'b1), .clk(multiplexer_3_out), .carry(S2_carry), .Q(S2_q));  // open: load, up, D
  Counter #(.max('h5), .width(4)) S1 (
    .clr(t_ff_1_q), .count(S2_carry), .clk(multiplexer_3_out), .carry(S1_carry), .Q(S1_q));  // open: load, up, D
  Counter #(.max('h9), .width(4)) TM2 (
    .up(not_2_out), .count(or_6_out), .clk(multiplexer_3_out), .carry(TM2_carry), .Q(TM2_q));  // open: clr, load, D
  Counter #(.max('h5), .width(4)) TM1 (
    .up(not_2_out), .count(or_7_out), .clk(multiplexer_3_out), .carry(TM1_carry), .Q(TM1_q));  // open: clr, load, D
  Counter #(.max('h9), .width(4)) TH2 (
    .load(or_11_out), .up(not_2_out), .count(or_8_out), .clk(multiplexer_3_out), .D(multiplexer_1_out),
    .carry(TH2_carry), .Q(TH2_q));  // open: clr
  Counter #(.max('h2), .width(4)) TH1 (
    .load(or_11_out), .up(not_2_out), .count(or_5_out), .clk(multiplexer_3_out), .D(multiplexer_2_out),
    .carry(TH1_carry), .Q(TH1_q));  // open: clr
  Multiplexer multiplexer_3 (.in0(counter_2_q[6]), .in1(counter_2_q[3]), .out(multiplexer_3_out), .sel(t_ff_1_q));
  and and_1 (and_1_out, and_8_out, TH2_carry);
  and and_2 (and_2_out, TH2_carry, Up_out, decoder_1_out0);
  and and_3 (and_3_out, decoder_1_out0, Down_out, nor_2_out);
  and and_4 (and_4_out, S2_carry, S1_carry);
  and and_5 (and_5_out, decoder_1_out1, or_4_out);
  nor nor_1 (nor_1_out, TM2_q[0], TM2_q[1], TM2_q[2], TM2_q[3]);
  and and_6 (and_6_out, TM2_carry, decoder_1_out1, Up_out);
  and and_7 (and_7_out, nor_1_out, decoder_1_out1, Down_out);
  and and_8 (and_8_out, TM1_carry, and_11_out);
  and and_9 (and_9_out, decoder_1_out0, or_4_out);
  nor nor_2 (nor_2_out, TH2_q[0], TH2_q[1], TH2_q[2], TH2_q[3]);
  or or_5 (or_5_out, and_1_out, and_2_out, and_3_out);
  and and_10 (and_10_out, and_17_out, not_1_out);
  or or_6 (or_6_out, and_4_out, and_5_out);
  or or_7 (or_7_out, and_6_out, and_11_out, and_7_out);
  or or_8 (or_8_out, and_8_out, and_9_out);
  and and_11 (and_11_out, and_4_out, TM2_carry);
  or or_9 (or_9_out, TH2_q[0], TH2_q[1], TH2_q[2], TH2_q[3]);
  or or_10 (or_10_out, TH1_q[0], TH1_q[1], TH1_q[2], TH1_q[3]);
  and and_12 (and_12_out, TH2_q[1], TH2_q[0]);
  and and_13 (and_13_out, and_8_out, and_12_out, TH1_carry);
  and and_14 (and_14_out, decoder_1_out0, and_12_out, Up_out, TH1_carry);
  nor nor_3 (nor_3_out, or_9_out, or_10_out);
  and and_15 (and_15_out, or_2_out, and_17_out);
  Counter #(.max('h3), .width(2)) counter_3 (
    .clk(clock_1_out), .Q(counter_3_q));  // open: clr, load, up, count, D, carry
  Decoder #(.select(2)) decoder_2 (
    .out0(decoder_2_out0), .out1(decoder_2_out1), .out2(decoder_2_out2), .out3(decoder_2_out3),
    .sel(counter_3_q), .en(1'b1));
  _7_Segment_Display u_7_segment_display_1 ();  // open: g, f, a, b, e, d, c, dp
  // BCD_to_7_Segment_decoder bcd_to_7_segment_decoder_1: pin names not known; wires that end beside it: bcd_to_7_segment_decoder_1_p1
  Multiplexer #(.width(4)) multiplexer_4 (
    .in1(multiplexer_6_out), .out(bcd_to_7_segment_decoder_1_p1), .sel(decoder_2_out0));  // open: in0
  or or_11 (or_11_out, and_13_out, and_16_out, and_14_out);
  and and_16 (and_16_out, nor_3_out, Down_out, decoder_1_out0);
  T_Flip_Flop t_ff_2 (.T(and_10_out), .clk(counter_2_q[3]), .Q(t_ff_2_q));  // open: Qn, reset, preset
  _7_Segment_Display u_7_segment_display_2 ();  // open: g, f, a, b, e, d, c, dp
  // BCD_to_7_Segment_decoder bcd_to_7_segment_decoder_2: pin names not known; wires that end beside it: bcd_to_7_segment_decoder_2_p1
  Multiplexer #(.width(4)) multiplexer_5 (
    .in1(multiplexer_6_out), .out(bcd_to_7_segment_decoder_2_p1), .sel(decoder_2_out1));  // open: in0
  Multiplexer #(.select(2), .width(4)) multiplexer_6 (
    .in0(multiplexer_7_out), .in1(multiplexer_9_out), .in2(multiplexer_10_out), .in3(multiplexer_13_out),
    .out(multiplexer_6_out), .sel(counter_3_q));
  Multiplexer #(.width(4)) multiplexer_7 (.in0(TH1_q), .in1(AH1_q), .out(multiplexer_7_out), .sel(or_3_out));
  Subtractor #(.width(4)) subtractor_1 (.a(AH1_q), .b(TH1_q), .out(subtractor_1_out));  // open: bin, bout
  T_Flip_Flop t_ff_3 (.T(and_15_out), .clk(counter_2_q[3]), .Q(t_ff_3_q));  // open: Qn, reset, preset
  _7_Segment_Display u_7_segment_display_3 ();  // open: g, f, a, b, e, d, c, dp
  _7_Segment_Display u_7_segment_display_4 ();  // open: g, f, a, b, e, d, c, dp
  // BCD_to_7_Segment_decoder bcd_to_7_segment_decoder_3: pin names not known; wires that end beside it: bcd_to_7_segment_decoder_3_p1
  // BCD_to_7_Segment_decoder bcd_to_7_segment_decoder_4: pin names not known; wires that end beside it: bcd_to_7_segment_decoder_4_p1
  Multiplexer #(.width(4)) multiplexer_8 (
    .in1(multiplexer_6_out), .out(bcd_to_7_segment_decoder_3_p1), .sel(decoder_2_out2));  // open: in0
  Multiplexer #(.width(4)) multiplexer_9 (.in0(TH2_q), .in1(AH2_q), .out(multiplexer_9_out), .sel(or_3_out));
  Multiplexer #(.width(4)) multiplexer_10 (.in0(TM1_q), .in1(AM1_q), .out(multiplexer_10_out), .sel(or_3_out));
  Subtractor #(.width(4)) subtractor_2 (.a(AH2_q), .b(TH2_q), .out(subtractor_2_out));  // open: bin, bout
  and and_17 (and_17_out, nor_4_out[0], nor_4_out[1], nor_4_out[2], nor_4_out[3]);
  LED led_1 (.in(multiplexer_11_out));
  Multiplexer multiplexer_11 (.in0(t_ff_2_q), .in1(1'b0), .out(multiplexer_11_out), .sel(t_ff_3_q));
  Multiplexer #(.width(4)) multiplexer_12 (
    .in1(multiplexer_6_out), .out(bcd_to_7_segment_decoder_4_p1), .sel(decoder_2_out3));  // open: in0
  Multiplexer #(.width(4)) multiplexer_13 (.in0(TM2_q), .in1(AM2_q), .out(multiplexer_13_out), .sel(or_3_out));
  Subtractor #(.width(4)) subtractor_3 (.a(AM1_q), .b(TM1_q), .out(subtractor_3_out));  // open: bin, bout
  assign nor_4_out = ~(subtractor_1_out | subtractor_2_out | subtractor_3_out | subtractor_4_out);  // NOR_Gate nor_4, 4 bits wide
  _7_Segment_Display u_7_segment_display_5 ();  // open: g, f, a, b, e, d, c, dp
  // BCD_to_7_Segment_decoder bcd_to_7_segment_decoder_5: pin names not known; wires that end beside it: S1_q
  Subtractor #(.width(4)) subtractor_4 (.a(TM2_q), .b(AM2_q), .out(subtractor_4_out));  // open: bin, bout
  _7_Segment_Display u_7_segment_display_6 ();  // open: g, f, a, b, e, d, c, dp
  // BCD_to_7_Segment_decoder bcd_to_7_segment_decoder_6: pin names not known; wires that end beside it: S2_q
  Multiplexer #(.width(4)) multiplexer_14 (.in0(4'b0011), .in1(4'b0000), .out(multiplexer_14_out), .sel(Up_out));
  Multiplexer #(.width(4)) multiplexer_15 (.in0(4'b0010), .in1(4'b0000), .out(multiplexer_15_out), .sel(Up_out));
  and and_18 (and_18_out, decoder_1_out3, Down_out);
  and and_19 (and_19_out, decoder_1_out3, Up_out);
  Counter #(.max('h9), .width(4)) AM2 (
    .up(Up_out), .count(or_12_out), .clk(counter_2_q[3]), .carry(AM2_carry), .Q(AM2_q));  // open: clr, load, D
  Counter #(.max('h5), .width(4)) AM1 (
    .up(Up_out), .count(or_15_out), .clk(counter_2_q[3]), .Q(AM1_q));  // open: clr, load, D, carry
  Counter #(.max('h9), .width(4)) AH2 (
    .load(or_16_out), .up(Up_out), .count(or_13_out), .clk(counter_2_q[3]), .D(multiplexer_14_out),
    .carry(AH2_carry), .Q(AH2_q));  // open: clr
  Counter #(.max('h2), .width(4)) AH1 (
    .load(or_16_out), .up(Up_out), .count(or_14_out), .clk(counter_2_q[3]), .D(multiplexer_15_out),
    .carry(AH1_carry), .Q(AH1_q));  // open: clr
  or or_12 (or_12_out, and_18_out, and_19_out);
  nor nor_5 (nor_5_out, AM2_q[0], AM2_q[1], AM2_q[2], AM2_q[3]);
  and and_20 (and_20_out, decoder_1_out2, Down_out);
  and and_21 (and_21_out, decoder_1_out2, Up_out);
  and and_22 (and_22_out, Up_out, AH2_carry, decoder_1_out2);
  and and_23 (and_23_out, decoder_1_out2, nor_7_out, Down_out);
  nor nor_6 (nor_6_out, AH1_q[0], AH1_q[1], AH1_q[2], AH1_q[3]);
  and and_24 (and_24_out, Up_out, AM2_carry, decoder_1_out3);
  and and_25 (and_25_out, decoder_1_out3, Down_out, nor_5_out);
  or or_13 (or_13_out, and_20_out, and_21_out);
  or or_14 (or_14_out, and_22_out, and_23_out);
  and and_26 (and_26_out, decoder_1_out2, Up_out, and_28_out, AH1_carry);
  and and_27 (and_27_out, Down_out, decoder_1_out2, nor_7_out, nor_6_out);
  or or_15 (or_15_out, and_24_out, and_25_out);
  and and_28 (and_28_out, AH2_q[0], AH2_q[1]);
  or or_16 (or_16_out, and_26_out, and_27_out);
  nor nor_7 (nor_7_out, AH2_q[0], AH2_q[1], AH2_q[2], AH2_q[3]);
endmodule
